# Fritzing sketch Walle (saved by Fritzing 0.9.4)

parts:
  Raspberry_Pi_1 = Raspberry Pi 3 [part_number=RPI-3-V1.2]
  18650_holder1 = 18650 holder [package="DIP (Dual Inline) [THT]"]
  18650_holder2 = 18650 holder [package="DIP (Dual Inline) [THT]"]
  18650_holder3 = 18650 holder [package="DIP (Dual Inline) [THT]"]
  Mod1 = 3S-BMS
  U1 = LM2596 step down module
  S1 = H-Bridge with L298N
  BATT1 = LiPoly Battery (1300mAh)  # not connected
  M1 = DC Motor
  M2 = DC Motor
  Компонент1 = 16-Channel 12-bit PWM Servo Driver - I2C [part_number=815]
  SPKR1 = Loudspeaker  # not connected
  Компонент3 = Adafruit USB DC Solar LiPo Charger [part_number="Adafruit #390"]  # not connected
  HC-SR04_Sensor_1 = HC-SR04 Ultrasonic Distance Sensor
  R1 = Resistor [tolerance=±5% resistance=330 package="0402 [SMD]"]
  J1 = Basic Servo  # not connected
  J2 = Basic Servo  # not connected
  J3 = Basic Servo  # not connected
  J4 = Basic Servo  # not connected
  J5 = Basic Servo  # not connected
  J6 = Basic Servo  # not connected
  J7 = Basic Servo  # not connected
  J8 = Basic Servo  # not connected
  J9 = Basic Servo  # not connected
  J10 = Basic Servo  # not connected
  J11 = Basic Servo  # not connected
  J12 = Basic Servo  # not connected
  J13 = Basic Servo  # not connected
  J14 = Basic Servo  # not connected
  J15 = Basic Servo  # not connected
  J16 = Basic Servo  # not connected
  MIC1 = Microphone  # not connected
  Power_plug1 = Power plug
  R2 = Resistor [tolerance=±5% resistance=470 package="0402 [SMD]"]  # not connected

nets:
  3V3: Raspberry_Pi_1.3v3, U1.OUT+, HC-SR04_Sensor_1.VCC
  N1: Raspberry_Pi_1.GPIO2, Компонент1.SDA
  N2: Raspberry_Pi_1.GPIO3, Компонент1.SCL
  N3: Raspberry_Pi_1.GPIO4, S1.IN1
  GND: Raspberry_Pi_1.GND, S1.GND, Компонент1.GND
  N4: Raspberry_Pi_1.GPIO17, S1.IN2
  N5: Raspberry_Pi_1.GPIO27, S1.IN3
  N6: Raspberry_Pi_1.GPIO22, S1.IN4
  N7: Raspberry_Pi_1.GPIO6, R1.Pin_1
  5V: Raspberry_Pi_1.5V, Компонент1.VCC
  N8: 18650_holder1.holder_+, Mod1.8.4V
  N9: 18650_holder1.holder_-, 18650_holder3.holder_+, Mod1.4.2V
  N10: 18650_holder2.holder_+, 18650_holder3.holder_-, Mod1.0V
  N11: 18650_holder2.holder_-, Mod1.12.6V
  N12: Mod1.-, U1.IN-, Power_plug1.GND
  N13: Mod1.+, U1.IN+, Power_plug1.VCC
  N14: S1.M1-01, M2.pin_2
  N15: S1.M1-02, M2.pin_1
  N16: S1.M2-01, M1.pin_1
  N17: S1.M2-02, M1.pin_2

notes:
  Для открытия переднего отсека
  Для движения рук вверх и вниз
  Для сжимания "клешней"
  Для движения глаз вверх вниз
  Для движения головы по двум осям
  Больше степеней свободы для рук
  Микромимика, если будет необходимо (моргания глаз, дополнительные эмоциональные реакции)
  Для питания мозгов, возможна замена на модуль зарядки от солнечной батареи
  Полимерный аккумулятор для ходовй части
  18650 для питания "мозгов"
  Микрофон и динамик для восприятия и реакции на голосовые команды
  Датчик растояния для объязда препятсвий
  Для двигателей могут понадобится редукторы
  Надо как-то питать, от бп например или от чего-то другого, но плата расчитана на 12В

custom parts:
  18650 holder: Акум формата 18650 в холдере
  3S-BMS: 3S-BMS LIPO battery charger / protection unit. Note pcb does not match the board as it will likely connect with wires, so pcb is 6 pads suitable for .1in header pins.
  LM2596 step down module: LM2596 DC-DC step down power supply module 3 A.
  H-Bridge with L298N: h-bridge
  LiPoly Battery (1300mAh): Lithium Ion Polymer Battery (1300mAh)
  16-Channel 12-bit PWM Servo Driver - I2C: You want to make a cool robot, maybe a hexapod walker, or maybe just a piece of art with a lot of moving parts. Or maybe you want to drive a lot of LEDs with precise PWM output. Using only two pins, control 16 free-running PWM outputs! You can even chain up 62 breakouts to control up to 992 PWM outputs.
  Adafruit USB DC Solar LiPo Charger: Make your projects to go green this summer with our specialized USB/Solar Lithium Ion Polymer Battery charger! This charger is a very unique design, perfect for outdoor projects, or DIY iPod chargers. We've spent over a year testing and tinkering with this charger to come up with a plug and play solution to charging batteries with the sun and we're really pleased with what we ended up with.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
